# Fritzing sketch main_board (saved by Fritzing 0.9.10b)
circuit board: 12.7cm x 3.81cm
breadboards: 1

parts:
  Part1 = Adafruit DRV8833 DC/Stepper Motor Driver [part_number="Adafruit #3297"]
  J1 = female pin header, 6 pins [form="♀ (female)"]
  J2 = female pin header, 8 pins [form="♀ (female)"]
  TOF1 = female pin header, 6 pins [form="♀ (female)"]
  TOF3 = female pin header, 6 pins [form="♀ (female)"]
  TOF2 = female pin header, 6 pins [form="♀ (female)"]

nets:
  N1: Part1.GND, J1.pin6, TOF1.pin4, TOF3.pin4, TOF2.pin4
  N2: Part1.AOUT2, J2.pin6
  N3: Part1.AOUT1, J2.pin5
  N4: Part1.BOUT1, J2.pin8
  N5: Part1.BOUT2, J2.pin7
  N6: Part1.BIN1, J1.pin5
  N7: Part1.BIN2, J1.pin4
  N8: Part1.!SLEEP, J1.pin3, TOF1.pin6, TOF3.pin6, TOF2.pin6
  N9: Part1.AIN2, J1.pin2
  N10: Part1.AIN1, J1.pin1
  N11: J2.pin1, TOF1.pin2, TOF2.pin2
  N12: J2.pin2, TOF1.pin1, TOF2.pin1
  N13: J2.pin3, TOF3.pin2
  N14: J2.pin4, TOF3.pin1

notes:
  AOUT1
  AOUT2
  BOUT2
  BOUT1
  AIN1
  AIN2
  3v3
  BIN2
  BIN1
  GND
  SCL1
  SDA1
  SCL2
  SDA2
  TOF1
  TOF2
  PalBot v0.1
  Ethan Look

custom parts:
  Adafruit DRV8833 DC/Stepper Motor Driver: Spin two DC motors or step one bi-polar or uni-polar stepper with up to 1.2A per channel using the DRV8833. This motor driver chip is a nice alternative to the TB6612 driver. Like that chip, you get 2 full H-bridges, but this chip is better for low voltage uses (can run from 2.7V up to 10.8V motor power) and has built in current limiting capability. We set it up for 1A current limiting so you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
