# Fritzing sketch vl53l0x_verification_diagram (saved by Fritzing 0.9.10b)
breadboards: 1

parts:
  Mod1 = Raspberry Pi 4B
  Part1 = Adafruit VL6180X Time of Flight Distance Sensor [part_number="Adafruit #3316"]

nets:
  3V3: Mod1.3V3, Part1.VIN
  N1: Mod1.GPIO2, Part1.SDA
  N2: Mod1.GPIO3, Part1.SCL
  GND: Mod1.GND, Part1.GND

custom parts:
  Adafruit VL6180X Time of Flight Distance Sensor: The VL6180X is a Time of Flight distance sensor like no other you've used! The sensor contains a very tiny invisible laser source, and a matching sensor. The VL6180X can detect the "time of flight", or how long the light has taken to bounce back to the sensor. Since it uses a very narrow light source, it is good for determining distance of only the surface directly in front of it. Unlike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
